# Fritzing sketch termistor1 (saved by Fritzing 0.8.5b)
breadboards: 1

parts:
  R1 = Resistor [tolerance=±5% resistance=1.1k package=THT]
  Part1 = Arduino Uno (Rev3) - ICSP
  R2 = Temperature Sensor (Thermistor) [thermistor_type=PTC package=THT]  # not connected

nets:
  N1: R1.Pin_0, Part1.5V
  N2: R1.Pin_1, Part1.A2
