# Fritzing sketch termistor2 (saved by Fritzing 0.8.5b)
breadboards: 1

parts:
  R1 = Resistor [tolerance=±5% resistance=1.1k package=THT]
  Part1 = Arduino Uno (Rev3) - ICSP
  R2 = Temperature Sensor (Thermistor) [thermistor_type=PTC package=THT]  # not connected
  R3 = Resistor [tolerance=±5% resistance=220 package=THT]
  LED1 = LED - 5mm [color="Green (565nm)" package="5 mm [THT]"]

nets:
  N1: R1.Pin_0, Part1.D7, R3.Pin_0
  N2: R1.Pin_1, Part1.A2
  N3: Part1.GND, LED1.anode
  N4: R3.Pin_1, LED1.cathode
